# Fritzing sketch schema (saved by Fritzing 0.9.4)

parts:
  Arduino_Nano_(168) = Arduino Nano (Rev3.0)
  R1 = Temperature Sensor (Thermistor) [thermistor_type=NTC package=THT]
  R2 = Resistor [tolerance=±5% resistance=10k package=THT]
  SSD1306_I2C_128X64 = OLED 128x64 I2C Monochrome Display
  R3 = Rotary Potentiometer (Large) [maximum_resistance=100kΩ package=THT]

nets:
  GND: Arduino_Nano_(168).GND, R1.pin_0, SSD1306_I2C_128X64.GND, R3.leg2
  N1: Arduino_Nano_(168).A5, SSD1306_I2C_128X64.SCK
  N2: Arduino_Nano_(168).A4, SSD1306_I2C_128X64.SDA
  N3: Arduino_Nano_(168).A1, R3.wiper
  N4: Arduino_Nano_(168).A0, R1.pin_1
  N5: R2.Pin_0, SSD1306_I2C_128X64.VDD, R3.leg1
